# Fritzing sketch EE3579_LAB2_Closed_Loop (saved by Fritzing 0.9.3b)
breadboards: 1

parts:
  U1 = 74HC04_HEX_INVERTER [package=dil14]
  IC2 = L293D [package=THT]
  M1 = DC Motor
  Part1 = Arduino Uno (Rev3)
  3-pins_Hall_Effect_Sensor1 = mystery part, 3 pins [chip_label="Hall Effect Sensor"]
  S1 = Pushbutton [package="[THT]"]
  S2 = Pushbutton [package="[THT]"]
  S3 = Pushbutton [package="[THT]"]
  S5 = Pushbutton [package="[THT]"]
  S4 = Pushbutton [package="[THT]"]

nets:
  GND: U1.GND, IC2.0V, Part1.GND, 3-pins_Hall_Effect_Sensor1.pin1, S1.Pin_3, S1.Pin_4, S2.Pin_3, S2.Pin_4, S3.Pin_3, S3.Pin_4, S5.Pin_3, S5.Pin_4, S4.Pin_3, S4.Pin_4
  N1: U1.6Y, IC2.In_3
  N2: U1.6A, IC2.In_4, Part1.D12/MISO
  VCC: U1.VCC, IC2.+Vmotor, IC2.+V, Part1.5V, 3-pins_Hall_Effect_Sensor1.pin2
  N3: IC2.Out_1_(_Controlled_by_Enable_1_), M1.pin_2
  N4: IC2.Out_2_(_Controlled_by_Enable_1_), M1.pin_1
  N5: IC2.Enable_2, Part1.D11_PWM/MOSI
  N6: Part1.D8, S5.Pin_1, S5.Pin_2
  N7: Part1.D3_PWM, 3-pins_Hall_Effect_Sensor1.pin3
  N8: Part1.D4, S1.Pin_1, S1.Pin_2
  N9: Part1.D5_PWM, S2.Pin_1, S2.Pin_2
  N10: Part1.D6_PWM, S3.Pin_1, S3.Pin_2
  N11: Part1.D7, S4.Pin_1, S4.Pin_2
