# Fritzing sketch EE3579_LAB2_EX1 (saved by Fritzing 0.9.3b)
breadboards: 1

parts:
  U1 = 74HC04_HEX_INVERTER [package=dil14]
  IC2 = L293D [package=THT]
  M1 = DC Motor
  Part1 = Arduino Uno (Rev3)
  R1 = Trimmer Potentiometer [maximum_resistance=10kΩ package=THT]
  3-pins_Hall_Effect_Sensor1 = mystery part, 3 pins [chip_label="Hall Effect Sensor"]

nets:
  GND: U1.GND, IC2.0V, Part1.GND, R1.leg1, 3-pins_Hall_Effect_Sensor1.pin1
  N1: U1.6Y, IC2.In_3
  N2: U1.6A, IC2.In_4, Part1.D12/MISO
  VCC: U1.VCC, IC2.+Vmotor, IC2.+V, Part1.5V, R1.leg2, 3-pins_Hall_Effect_Sensor1.pin2
  N3: IC2.Out_1_(_Controlled_by_Enable_1_), M1.pin_2
  N4: IC2.Out_2_(_Controlled_by_Enable_1_), M1.pin_1
  N5: IC2.Enable_2, Part1.D11_PWM/MOSI
  N6: Part1.A0, R1.wiper
  N7: Part1.D3_PWM, 3-pins_Hall_Effect_Sensor1.pin3
